# Fritzing sketch rasppi-cubesolver (saved by Fritzing 0.9.4)

parts:
  Squix1 = OLED 0.96" 128x64 I2C SSD1306
  Raspberry_Pi_1 = Raspberry Pi 3 [part_number=RPI-3-V1.2]
  Part1 = 16-Channel 12-bit PCA9685 PWM/Servo Driver
  J1 = Basic Servo
  J2 = Basic Servo
  J3 = Basic Servo
  J4 = Basic Servo
  S3 = Pushbutton [package=THT]
  S4 = Pushbutton [package=THT]
  S5 = Pushbutton [package=THT]

nets:
  VCC: Squix1.VCC, Raspberry_Pi_1.3v3, Part1.VCC
  GND: Squix1.GND, Raspberry_Pi_1.GND, Part1.GND, J1.gnd, J2.gnd, J3.gnd, J4.gnd, S3.leg0, S4.leg0, S5.leg0
  N1: Squix1.SCL, Raspberry_Pi_1.GPIO3, Part1.SCL
  N2: Squix1.SCA, Raspberry_Pi_1.GPIO2, Part1.SDA
  N3: Raspberry_Pi_1.GIPO17, S3.leg1
  N4: Raspberry_Pi_1.GIPO27, S4.leg1
  N5: Raspberry_Pi_1.GIPO22, S5.leg1
  N6: Part1.0, J1.pulse
  N7: Part1.1, J2.pulse
  N8: Part1.2, J4.pulse
  N9: Part1.3, J3.pulse
  VCC_2: Part1.V+, J1.vcc, J2.vcc, J3.vcc, J4.vcc

custom parts:
  16-Channel 12-bit PCA9685 PWM/Servo Driver: The Adafruit 16-Channel 12-bit PWM/Servo Driver will drive up to 16 servos over I2C with only 2 pins. The on-board PCA9685 PWM controller will drive all 16 channels simultaneously with no additional processing overhead. What's more, you can chain up to 62 of them to control up to 992 servos - all with the same 2 pins
